// Logisim project Group5_PartA.circ as structural Verilog: 7 circuits, main circuit Reg16bit
module Reg16bit (
  input  clk,
  input  Reset,
  input  OE,
  input  WE,
  input  [15:0] Din,
  output [15:0] Dout,
  output [15:0] Result,
  output [7:0] LSB,
  output [7:0] MSB
);

  Register #(.width(16)) register_1 (.D(Din), .en(WE), .clk(clk), .Q(Result), .clr(Reset));
  assign Dout = OE ? Result : 16'bz;  // Controlled_Buffer controlled_buffer_1
  BitSelector #(.group(8), .width(16)) bitselector_1 (.in(Result), .out(LSB), .sel(1'b0));
  BitSelector #(.group(8), .width(16)) bitselector_2 (.in(Result), .out(MSB), .sel(1'b1));

  // Notes on the sheet:
  //   constant value 0x0
  //   constant value 0x1
endmodule

module project_ro (
  input  [15:0] A,
  input  [15:0] B,
  input  [2:0] RU_Selector,
  output RU_Result
);

  wire comparator_1_eq, comparator_1_gt, comparator_1_lt, not_1_out, or_1_out, or_2_out;

  Comparator #(.width(16)) comparator_1 (
    .a(A), .b(B), .gt(comparator_1_gt), .eq(comparator_1_eq), .lt(comparator_1_lt));
  or or_1 (or_1_out, comparator_1_gt, comparator_1_eq);
  or or_2 (or_2_out, comparator_1_lt, comparator_1_eq);
  not not_1 (not_1_out, comparator_1_eq);
  Multiplexer #(.select(3)) multiplexer_1 (
    .in0(comparator_1_gt), .in1(comparator_1_eq), .in2(or_1_out), .in3(comparator_1_lt), .in4(or_2_out),
    .in5(not_1_out), .out(RU_Result), .sel(RU_Selector));  // open: in6, in7

  // Notes on the sheet:
  //   >
  //   >=
  //   <
  //   <=
  //   ==
  //   !-
endmodule

module project_ao (
  input  [15:0] A,
  input  [15:0] B,
  input  [3:0] AUselector,
  output [15:0] AU_Result,
  output [15:0] AU_Dout
);

  wire [15:0] adder_1_out, adder_2_out, and_1_out, divider_1_out, divider_1_rem, multiplexer_1_out,
       multiplier_1_out, negator_1_out, negator_2_out, not_1_out, or_1_out, shifter_1_out, shifter_2_out,
       shifter_3_out, shifter_4_out, xor_1_out;

  Adder #(.width(16)) adder_1 (.a(A), .b(A), .out(adder_1_out));  // open: cin, cout
  assign and_1_out = A & A;  // AND_Gate and_1, 16 bits wide
  assign or_1_out = A | A;  // OR_Gate or_1, 16 bits wide
  Divider #(.width(16)) divider_1 (.a(A), .b(A), .out(divider_1_out), .rem(divider_1_rem));  // open: upper
  Multiplier #(.width(16)) multiplier_1 (.a(A), .b(A), .out(multiplier_1_out));  // open: cin, cout
  assign not_1_out = ~A;  // NOT_Gate not_1, 16 bits wide
  assign xor_1_out = A ^ A;  // XOR_Gate xor_1, 16 bits wide
  Multiplexer #(.width(16)) multiplexer_1 (
    .in0(divider_1_out), .in1(divider_1_rem), .out(multiplexer_1_out), .sel(AUselector[0]));
  Adder #(.width(16)) adder_2 (.a(A), .b(not_1_out), .out(adder_2_out), .cin(1'b1));  // open: cout
  Shifter #(.width(16)) shifter_1 (.in(A), .\dist (4'b0010), .out(shifter_1_out));
  Shifter #(.width(16)) shifter_2 (.in(A), .\dist (4'b0010), .out(shifter_2_out));
  Negator #(.width(16)) negator_1 (.in(A), .out(negator_1_out));
  Negator #(.width(16)) negator_2 (.in(A), .out(negator_2_out));
  Shifter #(.width(16)) shifter_3 (.in(A), .\dist (4'b0010), .out(shifter_3_out));
  Shifter #(.width(16)) shifter_4 (.in(A), .\dist (4'b0010), .out(shifter_4_out));
  Multiplexer #(.select(4), .width(16)) multiplexer_2 (
    .in0(adder_1_out), .in1(and_1_out), .in2(or_1_out), .in3(xor_1_out), .in4(multiplexer_1_out),
    .in5(multiplexer_1_out), .in6(multiplier_1_out), .in7(adder_2_out), .in8(shifter_1_out),
    .in9(shifter_2_out), .in10(shifter_3_out), .in11(shifter_4_out), .in12(negator_1_out),
    .in13(negator_2_out), .out(AU_Dout), .sel(AUselector));  // open: in14, in15

  assign AU_Result = AU_Dout;
  assign B = A;

  // Notes on the sheet:
  //   16-BIT ALU
endmodule

module project_alu (
  input  [15:0] A,
  input  [15:0] B,
  input  [3:0] AU_selector,
  input  [2:0] RU_Selector,
  output [15:0] AU_Result,
  output [15:0] AU_Dout,
  output RU_Result
);

  project_ao project_ao_1 (.A(A), .B(B), .AUselector(AU_selector), .AU_Result(AU_Result), .AU_Dout(AU_Dout));
  project_ro project_ro_1 (.A(A), .B(B), .RU_Selector(RU_Selector), .RU_Result(RU_Result));

  // Notes on the sheet:
  //   16 BITS ALU
endmodule

module Datapath (
  input  [15:0] test_data1,
  input  in_2,
  input  in_3,
  input  in_4,
  input  in_5,
  input  [3:0] AU_SELECTOR,
  input  [2:0] RU_SELECTOR,
  output [15:0] out_8,
  output [15:0] out_9
);

  wire clock_1_out, undriven, undriven_2, undriven_3, undriven_4, undriven_5, undriven_6, undriven_7,
       undriven_8, undriven_9, undriven_10, undriven_11, undriven_12, undriven_13, undriven_14, undriven_15,
       undriven_16;
  wire [7:0] bitselector_1_out, MAR_dout;
  wire [15:0] A_result, ALU_au_dout, B_result, IR_dout, MBR_dout, MBR_result;

  Clock clock_1 (.out(clock_1_out));
  BitSelector #(.group(8), .width(16)) bitselector_1 (.in(IR_dout), .out(bitselector_1_out), .sel(1'b0));
  Reg16bit IR (.clk(clock_1_out), .Din(ALU_au_dout), .Dout(IR_dout));  // open: Reset, OE, WE, Result, LSB, MSB
  Reg16bit A (
    .clk(clock_1_out), .OE(in_4), .WE(in_5), .Din(ALU_au_dout), .Dout(out_8), .Result(A_result));  // open: Reset, LSB, MSB
  Reg16bit B (.clk(clock_1_out), .Din(ALU_au_dout), .Result(B_result));  // open: Reset, OE, WE, Dout, LSB, MSB
  project_alu ALU (
    .A(A_result), .B(B_result), .AU_selector(AU_SELECTOR), .RU_Selector(RU_SELECTOR), .AU_Result(out_9),
    .AU_Dout(ALU_au_dout));  // open: RU_Result
  LED led_1 (.in(ALU_au_dout[15]));
  LED led_2 (.in(ALU_au_dout[14]));
  LED led_3 (.in(ALU_au_dout[13]));
  LED led_4 (.in(ALU_au_dout[12]));
  assign ALU_au_dout = in_2 ? test_data1 : 16'bz;  // Controlled_Buffer controlled_buffer_1
  LED led_5 (.in(ALU_au_dout[11]));
  LED led_6 (.in(ALU_au_dout[10]));
  LED led_7 (.in(ALU_au_dout[9]));
  LED led_8 (.in(ALU_au_dout[8]));
  LED led_9 (.in(ALU_au_dout[7]));
  LED led_10 (.in(ALU_au_dout[6]));
  LED led_11 (.in(ALU_au_dout[5]));
  LED led_12 (.in(ALU_au_dout[4]));
  LED led_13 (.in(ALU_au_dout[3]));
  LED led_14 (.in(ALU_au_dout[2]));
  LED led_15 (.in(ALU_au_dout[1]));
  LED led_16 (.in(ALU_au_dout[0]));
  assign ALU_au_dout = in_3 ? MBR_dout : 16'bz;  // Controlled_Buffer controlled_buffer_2
  Reg16bit Output_Register (
    .clk(clock_1_out), .Din(ALU_au_dout), .Dout(ALU_au_dout));  // open: Reset, OE, WE, Result, LSB, MSB
  Reg8bit MAR (.clk(clock_1_out), .Din(bitselector_1_out), .Dout(MAR_dout));  // open: Reset, OE, we, Result, LSB, MSB
  Reg16bit MBR (
    .clk(clock_1_out), .Din(ALU_au_dout), .Dout(MBR_dout), .Result(MBR_result));  // open: Reset, OE, WE, LSB, MSB
  LED led_17 (.in(undriven));
  LED led_18 (.in(undriven_2));
  LED led_19 (.in(undriven_3));
  LED led_20 (.in(undriven_4));
  LED led_21 (.in(undriven_5));
  LED led_22 (.in(undriven_6));
  LED led_23 (.in(undriven_7));
  LED led_24 (.in(undriven_8));
  LED led_25 (.in(undriven_9));
  LED led_26 (.in(undriven_10));
  LED led_27 (.in(undriven_11));
  LED led_28 (.in(undriven_12));
  LED led_29 (.in(undriven_13));
  LED led_30 (.in(undriven_14));
  LED led_31 (.in(undriven_15));
  LED led_32 (.in(undriven_16));

  // Notes on the sheet:
  //   INTERNAL ADDRESS BUS
  //   INTERNAL DATA BUS
  //   EXTERNAL ADDRESS BUS
  //   EXTERNAL DATA BUS
endmodule

module cpu2 (
  input  in_1,
  input  [3:0] in_2,
  input  [7:0] Test_data,
  input  OE,
  input  [1:0] AU_SELECTOR,
  input  [2:0] LU_SELECTOR,
  output [3:0] out_7,
  output [3:0] counter_content,
  output [7:0] out_9,
  output [7:0] out_10,
  output [7:0] out_11,
  output [7:0] out_12,
  output COUT,
  output [7:0] AU_RESULT,
  output ALU_RESULT,
  output [2:0] SC_O
);

  wire A_p2, alu_1_p3, alu_1_p4, B_p2, CLK_out, cu_1_p8, cu_1_p9, cu_1_p10, cu_1_p11, cu_1_p13, IR_p2, IR_p3,
       MAR_p2, MAR_p3, MBR_p2, MBR_p3, OUTPUT_REGISTER_p2, OUTPUT_REGISTER_p3;
  wire [3:0] bitselector_2_out, controlled_buffer_1_out, decimal_decoder_1_p1_3, decimal_decoder_2_p1_3,
       decimal_decoder_4_p2_3, MAR_p5;
  wire [7:0] bit_extender_1_out, bit_extender_2_out, IR_p4, IR_p6, ram_1_dout;
  wire [15:0] decimal_decoder_1_p1, decimal_decoder_2_p1, decimal_decoder_3_p2, decimal_decoder_3_p2_2,
       decimal_decoder_4_p2, decimal_decoder_5_p2, decimal_decoder_5_p2_2;
  wire [27:16] decimal_decoder_1_p1_2, decimal_decoder_2_p1_2, decimal_decoder_4_p2_2;

  Clock CLK (.out(CLK_out));
  Counter #(.max('h3), .width(4)) PC (
    .count(cu_1_p9), .clk(CLK_out), .D(controlled_buffer_1_out), .Q(counter_content));  // open: clr, load, up, carry
  // reg8bits IR: pin names not known; wires that end beside it: CLK_out, IR_p2, IR_p3, IR_p4, out_9, IR_p6
  assign controlled_buffer_1_out = cu_1_p8 ? counter_content : 4'bz;  // Controlled_Buffer controlled_buffer_1
  // reg8bits A: pin names not known; wires that end beside it: CLK_out, A_p2, IR_p4, out_11, out_11
  // ALU alu_1: pin names not known; wires that end beside it: AU_SELECTOR, out_11, alu_1_p3, alu_1_p4, LU_SELECTOR, COUT, AU_RESULT, IR_p4, ALU_RESULT
  // reg8bits B: pin names not known; wires that end beside it: CLK_out, B_p2, IR_p4, alu_1_p4, alu_1_p4
  BitSelector #(.group(4)) bitselector_1 (.in(IR_p6), .out(controlled_buffer_1_out), .sel(1'b0));
  assign bit_extender_1_out = {{4{1'b0}}, counter_content};  // Bit_Extender bit_extender_1
  // Decimal_Decoder decimal_decoder_1: pin names not known; wires that end beside it: {decimal_decoder_1_p1_3, decimal_decoder_1_p1_2, decimal_decoder_1_p1}
  _7_Segment_Display u_7_segment_display_1 (
    .g(decimal_decoder_1_p1[15]), .f(decimal_decoder_1_p1[14]), .a(decimal_decoder_1_p1[13]),
    .b(decimal_decoder_1_p1[12]), .e(decimal_decoder_1_p1_3[3]), .d(decimal_decoder_1_p1_3[2]),
    .c(decimal_decoder_1_p1_3[1]), .dp(decimal_decoder_1_p1_3[0]));
  _7_Segment_Display u_7_segment_display_2 (
    .g(decimal_decoder_1_p1[11]), .f(decimal_decoder_1_p1[10]), .a(decimal_decoder_1_p1[9]),
    .b(decimal_decoder_1_p1[8]), .e(decimal_decoder_1_p1_2[27]), .d(decimal_decoder_1_p1_2[26]),
    .c(decimal_decoder_1_p1_2[25]), .dp(decimal_decoder_1_p1_2[24]));
  // Decimal_Decoder decimal_decoder_2: pin names not known; wires that end beside it: {decimal_decoder_2_p1_3, decimal_decoder_2_p1_2, decimal_decoder_2_p1}
  _7_Segment_Display u_7_segment_display_3 (
    .g(decimal_decoder_2_p1[15]), .f(decimal_decoder_2_p1[14]), .a(decimal_decoder_2_p1[13]),
    .b(decimal_decoder_2_p1[12]), .e(decimal_decoder_2_p1_3[3]), .d(decimal_decoder_2_p1_3[2]),
    .c(decimal_decoder_2_p1_3[1]), .dp(decimal_decoder_2_p1_3[0]));
  _7_Segment_Display u_7_segment_display_4 (
    .g(decimal_decoder_2_p1[11]), .f(decimal_decoder_2_p1[10]), .a(decimal_decoder_2_p1[9]),
    .b(decimal_decoder_2_p1[8]), .e(decimal_decoder_2_p1_2[27]), .d(decimal_decoder_2_p1_2[26]),
    .c(decimal_decoder_2_p1_2[25]), .dp(decimal_decoder_2_p1_2[24]));
  // Decimal_Decoder decimal_decoder_3: pin names not known; wires that end beside it: bit_extender_1_out, {decimal_decoder_3_p2_2, decimal_decoder_3_p2}
  _7_Segment_Display u_7_segment_display_5 (
    .g(decimal_decoder_3_p2[3]), .f(decimal_decoder_3_p2[2]), .a(decimal_decoder_3_p2[1]),
    .b(decimal_decoder_3_p2[0]), .e(decimal_decoder_3_p2_2[3]), .d(decimal_decoder_3_p2_2[2]),
    .c(decimal_decoder_3_p2_2[1]), .dp(decimal_decoder_3_p2_2[0]));
  _7_Segment_Display u_7_segment_display_6 (
    .g(decimal_decoder_1_p1[7]), .f(decimal_decoder_1_p1[6]), .a(decimal_decoder_1_p1[5]),
    .b(decimal_decoder_1_p1[4]), .e(decimal_decoder_1_p1_2[23]), .d(decimal_decoder_1_p1_2[22]),
    .c(decimal_decoder_1_p1_2[21]), .dp(decimal_decoder_1_p1_2[20]));
  _7_Segment_Display u_7_segment_display_7 (
    .g(decimal_decoder_2_p1[7]), .f(decimal_decoder_2_p1[6]), .a(decimal_decoder_2_p1[5]),
    .b(decimal_decoder_2_p1[4]), .e(decimal_decoder_2_p1_2[23]), .d(decimal_decoder_2_p1_2[22]),
    .c(decimal_decoder_2_p1_2[21]), .dp(decimal_decoder_2_p1_2[20]));
  LED led_1 (.in(IR_p4[7]));
  assign IR_p4 = OE ? Test_data : 8'bz;  // Controlled_Buffer controlled_buffer_2
  _7_Segment_Display u_7_segment_display_8 (
    .g(decimal_decoder_1_p1[3]), .f(decimal_decoder_1_p1[2]), .a(decimal_decoder_1_p1[1]),
    .b(decimal_decoder_1_p1[0]), .e(decimal_decoder_1_p1_2[19]), .d(decimal_decoder_1_p1_2[18]),
    .c(decimal_decoder_1_p1_2[17]), .dp(decimal_decoder_1_p1_2[16]));
  _7_Segment_Display u_7_segment_display_9 (
    .g(decimal_decoder_2_p1[3]), .f(decimal_decoder_2_p1[2]), .a(decimal_decoder_2_p1[1]),
    .b(decimal_decoder_2_p1[0]), .e(decimal_decoder_2_p1_2[19]), .d(decimal_decoder_2_p1_2[18]),
    .c(decimal_decoder_2_p1_2[17]), .dp(decimal_decoder_2_p1_2[16]));
  LED led_2 (.in(IR_p4[6]));
  LED led_3 (.in(IR_p4[5]));
  LED led_4 (.in(IR_p4[4]));
  LED led_5 (.in(IR_p4[3]));
  LED led_6 (.in(IR_p4[2]));
  LED led_7 (.in(IR_p4[1]));
  LED led_8 (.in(IR_p4[0]));
  assign IR_p4 = cu_1_p13 ? out_10 : 8'bz;  // Controlled_Buffer controlled_buffer_3
  // reg4bits MAR: pin names not known; wires that end beside it: controlled_buffer_1_out, MAR_p2, MAR_p3, CLK_out, MAR_p5, out_7
  Counter #(.max('h5), .width(3)) STEP_COUNTER (.clk(CLK_out), .Q(SC_O));  // open: clr, load, up, count, D, carry
  _7_Segment_Display u_7_segment_display_10 (
    .g(decimal_decoder_4_p2[15]), .f(decimal_decoder_4_p2[14]), .a(decimal_decoder_4_p2[13]),
    .b(decimal_decoder_4_p2[12]), .e(decimal_decoder_4_p2_3[3]), .d(decimal_decoder_4_p2_3[2]),
    .c(decimal_decoder_4_p2_3[1]), .dp(decimal_decoder_4_p2_3[0]));
  BitSelector #(.group(4)) bitselector_2 (.in(out_9), .out(bitselector_2_out), .sel(1'b1));
  // reg8bits MBR: pin names not known; wires that end beside it: CLK_out, MBR_p2, MBR_p3, IR_p4, out_10, IR_p4
  // reg8bits OUTPUT_REGISTER: pin names not known; wires that end beside it: CLK_out, OUTPUT_REGISTER_p2, OUTPUT_REGISTER_p3, IR_p4, out_12, IR_p4
  // Decimal_Decoder decimal_decoder_4: pin names not known; wires that end beside it: out_12, {decimal_decoder_4_p2_3, decimal_decoder_4_p2_2, decimal_decoder_4_p2}
  _7_Segment_Display u_7_segment_display_11 (
    .g(decimal_decoder_4_p2[11]), .f(decimal_decoder_4_p2[10]), .a(decimal_decoder_4_p2[9]),
    .b(decimal_decoder_4_p2[8]), .e(decimal_decoder_4_p2_2[27]), .d(decimal_decoder_4_p2_2[26]),
    .c(decimal_decoder_4_p2_2[25]), .dp(decimal_decoder_4_p2_2[24]));
  _7_Segment_Display u_7_segment_display_12 (
    .g(decimal_decoder_4_p2[7]), .f(decimal_decoder_4_p2[6]), .a(decimal_decoder_4_p2[5]),
    .b(decimal_decoder_4_p2[4]), .e(decimal_decoder_4_p2_2[23]), .d(decimal_decoder_4_p2_2[22]),
    .c(decimal_decoder_4_p2_2[21]), .dp(decimal_decoder_4_p2_2[20]));
  _7_Segment_Display u_7_segment_display_13 (
    .g(decimal_decoder_4_p2[3]), .f(decimal_decoder_4_p2[2]), .a(decimal_decoder_4_p2[1]),
    .b(decimal_decoder_4_p2[0]), .e(decimal_decoder_4_p2_2[19]), .d(decimal_decoder_4_p2_2[18]),
    .c(decimal_decoder_4_p2_2[17]), .dp(decimal_decoder_4_p2_2[16]));
  assign bit_extender_2_out = {{5{1'b0}}, SC_O};  // Bit_Extender bit_extender_2
  assign MAR_p5 = in_1 ? in_2 : 4'bz;  // Controlled_Buffer controlled_buffer_4
  LED led_9 (.in(IR_p4[7]));
  LED led_10 (.in(IR_p4[6]));
  LED led_11 (.in(IR_p4[5]));
  // CU cu_1: pin names not known; wires that end beside it: bitselector_2_out[3], bitselector_2_out[2], bitselector_2_out[1], bitselector_2_out[0], SC_O[2], SC_O[1], SC_O[0], cu_1_p8, cu_1_p9, cu_1_p10, cu_1_p11, MBR_p3, cu_1_p13, MBR_p2, IR_p3, IR_p2, MAR_p2
  // Decimal_Decoder decimal_decoder_5: pin names not known; wires that end beside it: bit_extender_2_out, {decimal_decoder_5_p2_2, decimal_decoder_5_p2}, MAR_p3, alu_1_p3, A_p2, B_p2, OUTPUT_REGISTER_p2, OUTPUT_REGISTER_p3
  LED led_12 (.in(IR_p4[4]));
  _7_Segment_Display u_7_segment_display_14 (
    .g(decimal_decoder_5_p2[3]), .f(decimal_decoder_5_p2[2]), .a(decimal_decoder_5_p2[1]),
    .b(decimal_decoder_5_p2[0]), .e(decimal_decoder_5_p2_2[3]), .d(decimal_decoder_5_p2_2[2]),
    .c(decimal_decoder_5_p2_2[1]), .dp(decimal_decoder_5_p2_2[0]));
  LED led_13 (.in(IR_p4[3]));
  LED led_14 (.in(IR_p4[2]));
  LED led_15 (.in(IR_p4[1]));
  LED led_16 (.in(IR_p4[0]));
  RAM #(.addrWidth(4), .enables("line")) ram_1 (
    .addr(MAR_p5), .we(cu_1_p10), .clk(CLK_out), .din(IR_p4), .dout(ram_1_dout));
  assign IR_p4 = cu_1_p11 ? ram_1_dout : 8'bz;  // Controlled_Buffer controlled_buffer_5

  // Notes on the sheet:
  //   OE
  //   WE
  //   INTERNAL ADDRESS BUS
  //   D7
  //   D5
  //   D6
  //   D4
  //   D3
  //   D2
  //   D1
  //   OE
  //   WE
  //   INTERNAL DATA BUS
  //   D0
  //   EXTERNAL ADDRESS BUS
  //   oe_test
  //   D7
  //   D5
  //   D6
  //   D4
  //   D3
  //   D2
  //   D1
  //   WE
  //   EXTERNAL DATA BUS
  //   D0
  //   OE
endmodule

module Reg8bit (
  input  clk,
  input  Reset,
  input  OE,
  input  we,
  input  [7:0] Din,
  output [7:0] Dout,
  output [7:0] Result,
  output [7:0] LSB,
  output [7:0] MSB
);

  Register register_1 (.D(Din), .en(we), .clk(clk), .Q(Result), .clr(Reset));
  assign Dout = OE ? Result : 8'bz;  // Controlled_Buffer controlled_buffer_1
  BitSelector #(.group(8)) bitselector_1 (.in(Result), .out(LSB), .sel(1'b0));
  BitSelector #(.group(8)) bitselector_2 (.in(Result), .out(MSB), .sel(1'b1));

  // Notes on the sheet:
  //   constant value 0x0
  //   constant value 0x1
endmodule
